# Fritzing sketch PI0108.rev.1.0.1 (saved by Fritzing 0.9.3b)
breadboards: 1

parts:
  Part1 = Arduino Nano (Rev3.0) (ICSP)
  R3 = Resistor [tolerance=±5% resistance=220 package=THT]
  Button_1 = Pushbutton [package="[THT]"]
  LED8 = LED - 5mm [color="Red (633nm)" package="5 mm [THT]"]
  Button_2 = Pushbutton [package="[THT]"]
  LED9 = LED - 5mm [color="Red (633nm)" package="5 mm [THT]"]
  R4 = Resistor [tolerance=±5% resistance=220 package=THT]
  Button_3 = Pushbutton [package="[THT]"]
  LED10 = LED - 5mm [color="Red (633nm)" package="5 mm [THT]"]
  R5 = Resistor [tolerance=±5% resistance=220 package=THT]
  Button_4 = Pushbutton [package="[THT]"]
  LED11 = LED - 5mm [color="Red (633nm)" package="5 mm [THT]"]
  R6 = Resistor [tolerance=±5% resistance=220 package=THT]
  Button_5 = Pushbutton [package="[THT]"]
  Button_6 = Pushbutton [package="[THT]"]
  Button_7 = Pushbutton [package="[THT]"]
  Button_8 = Pushbutton [package="[THT]"]
  LED12 = LED - 5mm [color="Red (633nm)" package="5 mm [THT]"]
  LED13 = LED - 5mm [color="Red (633nm)" package="5 mm [THT]"]
  LED14 = LED - 5mm [color="Red (633nm)" package="5 mm [THT]"]
  LED15 = LED - 5mm [color="Red (633nm)" package="5 mm [THT]"]
  R7 = Resistor [tolerance=±5% resistance=220 package=THT]
  R8 = Resistor [tolerance=±5% resistance=220 package=THT]
  R9 = Resistor [tolerance=±5% resistance=220 package=THT]
  R10 = Resistor [tolerance=±5% resistance=220 package=THT]

nets:
  N1: Part1.D2, Button_1.Pin_1, Button_1.Pin_2, Button_2.Pin_2, Button_3.Pin_2, Button_4.Pin_2, Button_5.Pin_2, Button_6.Pin_1, Button_6.Pin_2, Button_7.Pin_2, Button_8.Pin_1
  N2: Part1.D3, R3.Pin_1
  N3: Part1.D4, R4.Pin_1
  N4: Part1.D5, R5.Pin_1
  N5: Part1.D6, R6.Pin_1
  N6: Part1.D7, R10.Pin_1
  N7: Part1.D8, R7.Pin_1
  N8: Part1.D9, R9.Pin_1
  N9: Part1.D10, R8.Pin_1
  N10: Part1.D12/MISO, LED8.cathode, LED9.cathode, LED10.cathode, LED11.cathode, LED12.cathode, LED13.cathode, LED14.cathode, LED15.cathode
  N11: R3.Pin_0, Button_1.Pin_3
  N12: Button_2.Pin_3, LED9.anode, R4.Pin_0
  N13: Button_3.Pin_3, LED10.anode, R5.Pin_0
  N14: Button_4.Pin_3, LED11.anode, R6.Pin_0
  N15: Button_5.Pin_3, LED12.anode, R7.Pin_0
  N16: Button_6.Pin_3, LED13.anode, R9.Pin_0
  N17: Button_7.Pin_3, LED14.anode, R8.Pin_0
  N18: Button_8.Pin_3, LED15.anode, R10.Pin_0
